// Logisim project jrmips.circ as structural Verilog: 11 circuits, main circuit main
module main (
);

  wire ALU_branch, and_1_out, Br, Clock_out, Decoder_halt, Decoder_put, Decoder_regwrite, Fields_subop,
       HILOEnable, Jr, MemWrite, not_1_out;
  wire [2:0] ALUOp, Decoder_writemux, Fields_rs, Fields_rt;
  wire [3:0] Fields_opcode, Last_Put_Saved_q, Last_Put_Saved_q_2, Last_Put_Saved_q_3, Last_Put_Saved_q_4;
  wire [7:0] bit_extender_3_out, bit_extender_4_out, Fields_immediate, multiplexer_1_out, multiplexer_2_out,
       PC_1, PC_q;
  wire [15:0] ALU_hi, ALU_result, bit_extender_1_out, bit_extender_2_out, HI_q, LO_q, MemData,
       multiplexer_3_out, RegisterFile_readdata1_output, RegisterFile_readdata2_output, rom_1_data;

  Clock Clock (.out(Clock_out));
  Hex_Digit_Display hex_digit_display_1 (.value(Last_Put_Saved_q_4));  // open: dp
  not not_1 (not_1_out, Decoder_halt);
  Hex_Digit_Display hex_digit_display_2 (.value(Last_Put_Saved_q_3));  // open: dp
  Hex_Digit_Display hex_digit_display_3 (.value(Last_Put_Saved_q_2));  // open: dp
  Register PC (.D(multiplexer_2_out), .en(not_1_out), .Q(PC_q), .clk(Clock_out));  // open: clr
  ROM #(.dataWidth(16)) rom_1 (.addr(PC_q), .data(rom_1_data), .sel(1'b1));
  Hex_Digit_Display hex_digit_display_4 (.value(Last_Put_Saved_q));  // open: dp
  Fields Fields (
    .Instruction(rom_1_data), .Rs(Fields_rs), .Rt(Fields_rt), .Opcode(Fields_opcode),
    .Immediate(Fields_immediate), .Subop(Fields_subop));
  Decoder Decoder (
    .Opcode(Fields_opcode), .Subop(Fields_subop), .RegWrite(Decoder_regwrite), .ALUOp(ALUOp),
    .Put(Decoder_put), .WriteMUX(Decoder_writemux), .HiLoC(HILOEnable), .MemWrite(MemWrite),
    .Halt(Decoder_halt), .JR(Jr), .BR(Br));
  Register #(.width(16)) Last_Put_Saved (
    .D(RegisterFile_readdata1_output), .en(Decoder_put),
    .Q({Last_Put_Saved_q_4, Last_Put_Saved_q_3, Last_Put_Saved_q_2, Last_Put_Saved_q}), .clk(Clock_out));  // open: clr
  Adder adder_1 (.a(PC_q), .b(8'h1), .out(PC_1), .cin(1'b0));  // open: cout
  Multiplexer #(.width(8), .disabled(0), .enable("false")) multiplexer_1 (
    .in0(PC_1), .in1(Fields_immediate), .out(multiplexer_1_out), .sel(and_1_out));
  assign bit_extender_1_out = {{8{1'b0}}, Fields_immediate};  // Bit_Extender bit_extender_1
  LED led_1 (.in(Decoder_halt));
  Multiplexer #(.width(8), .disabled(0), .enable("false")) multiplexer_2 (
    .in0(multiplexer_1_out), .in1(bit_extender_3_out), .out(multiplexer_2_out), .sel(Jr));
  Multiplexer #(.select(3), .width(16), .enable("false")) multiplexer_3 (
    .in0(ALU_result), .in1(bit_extender_1_out), .in2(bit_extender_2_out), .in3(MemData), .in4(LO_q),
    .in5(HI_q), .out(multiplexer_3_out), .sel(Decoder_writemux));  // open: in6, in7
  assign bit_extender_2_out = {{8{1'b0}}, PC_1};  // Bit_Extender bit_extender_2
  Bit_Extender #(.in_width(16), .out_width(8)) bit_extender_3 (
    .in(RegisterFile_readdata1_output), .out(bit_extender_3_out));
  RegisterFile RegisterFile (
    .WriteData_Input(multiplexer_3_out), .WriteEnable_Input(Decoder_regwrite),
    .WriteRegister_Input(Fields_rs), .ReadData2_Output(RegisterFile_readdata2_output),
    .ReadRegister2_Input(Fields_rt), .ReadData1_Output(RegisterFile_readdata1_output),
    .ReadRegister1_Input(Fields_rs), .Clock(Clock_out));
  and and_1 (and_1_out, ALU_branch, Br);
  ALU ALU (
    .rs(RegisterFile_readdata1_output), .rt(RegisterFile_readdata2_output), .Opcode(ALUOp),
    .Result(ALU_result), .HI(ALU_hi), .Immediate(Fields_immediate), .Branch(ALU_branch));
  Bit_Extender #(.in_width(16), .out_width(8)) bit_extender_4 (
    .in(RegisterFile_readdata2_output), .out(bit_extender_4_out));
  RAM #(.dataWidth(16), .bus("separate")) ram_1 (
    .addr(bit_extender_4_out), .din(RegisterFile_readdata1_output), .data(MemData), .str(MemWrite),
    .sel(1'b1), .clk(Clock_out), .ld(1'b1));  // open: clr
  Register #(.width(16)) LO (.D(ALU_result), .en(HILOEnable), .Q(LO_q), .clk(Clock_out));  // open: clr
  Register #(.width(16)) HI (.D(ALU_hi), .en(HILOEnable), .Q(HI_q), .clk(Clock_out));  // open: clr

  // Notes on the sheet:
  //   Jennifer Bramson
  //   jib41@pitt.edu
  //   Instuction Memory
  //   Hex Display
  //   contents of rom_1 (hex, n*v repeats v):
  //   f00a 201 a200 8030 100a a000 9626 f8c8 a800 1821 a800 f002 f20e 2200 a200 f00c 2201 a200 7a30 fa0a
  //   c741 7c00 cf40 ee00 b000
  //   JR
  //   Branch
  //   Halt Light
  //   WriteData
  //   Data Memory
endmodule

module RegisterFile (
  input  [15:0] WriteData_Input,
  input  [2:0] ReadRegister2_Input,
  input  WriteEnable_Input,
  input  [2:0] WriteRegister_Input,
  input  [2:0] ReadRegister1_Input,
  input  Clock,
  output [15:0] ReadData2_Output,
  output [15:0] ReadData1_Output
);

  wire decoder_1_out0, decoder_1_out1, decoder_1_out2, decoder_1_out3, decoder_1_out4, decoder_1_out5,
       decoder_1_out6, decoder_1_out7;
  wire [15:0] Register0_q, Register1_q, Register2_q, Register3_q, Register4_q, Register5_q, Register6_q,
       Register7_q;

  Decoder_part #(.select(3), .disabled(0)) decoder_1 (
    .out0(decoder_1_out0), .out1(decoder_1_out1), .out2(decoder_1_out2), .out3(decoder_1_out3),
    .out4(decoder_1_out4), .out5(decoder_1_out5), .out6(decoder_1_out6), .out7(decoder_1_out7),
    .sel(WriteRegister_Input), .en(WriteEnable_Input));
  Register #(.width(16)) Register0 (
    .D(WriteData_Input), .en(decoder_1_out0), .Q(Register0_q), .clk(Clock));  // open: clr
  Register #(.width(16)) Register1 (
    .D(WriteData_Input), .en(decoder_1_out1), .Q(Register1_q), .clk(Clock));  // open: clr
  Register #(.width(16)) Register2 (
    .D(WriteData_Input), .en(decoder_1_out2), .Q(Register2_q), .clk(Clock));  // open: clr
  Register #(.width(16)) Register3 (
    .D(WriteData_Input), .en(decoder_1_out3), .Q(Register3_q), .clk(Clock));  // open: clr
  Register #(.width(16)) Register4 (
    .D(WriteData_Input), .en(decoder_1_out4), .Q(Register4_q), .clk(Clock));  // open: clr
  Register #(.width(16)) Register5 (
    .D(WriteData_Input), .en(decoder_1_out5), .Q(Register5_q), .clk(Clock));  // open: clr
  Register #(.width(16)) Register6 (
    .D(WriteData_Input), .en(decoder_1_out6), .Q(Register6_q), .clk(Clock));  // open: clr
  Register #(.width(16)) Register7 (
    .D(WriteData_Input), .en(decoder_1_out7), .Q(Register7_q), .clk(Clock));  // open: clr
  Multiplexer #(.select(3), .width(16), .disabled(0), .enable("false")) multiplexer_1 (
    .in0(Register0_q), .in1(Register1_q), .in2(Register2_q), .in3(Register3_q), .in4(Register4_q),
    .in5(Register5_q), .in6(Register6_q), .in7(Register7_q), .out(ReadData2_Output), .sel(ReadRegister2_Input));
  Multiplexer #(.select(3), .width(16), .disabled(0), .enable("false")) multiplexer_2 (
    .in0(Register0_q), .in1(Register1_q), .in2(Register2_q), .in3(Register3_q), .in4(Register4_q),
    .in5(Register5_q), .in6(Register6_q), .in7(Register7_q), .out(ReadData1_Output), .sel(ReadRegister1_Input));
endmodule

module Decoder (
  input  [3:0] Opcode,
  input  Subop,
  output RegWrite,
  output [2:0] WriteMUX,
  output [2:0] ALUOp,
  output Put,
  output Halt,
  output HiLoC,
  output MemWrite,
  output BR,
  output JR
);

  RegWriteC RegWriteC (.Opcode(Opcode), .Subop(Subop), .RegWrite(RegWrite), .WriteMUX(WriteMUX));
  ALUOpC ALUOpC (.Opcode(Opcode), .Subop(Subop), .ALUop(ALUOp));
  Halt_Put Halt_Put (.Opcode(Opcode), .Put(Put), .Halt(Halt));
  HILOC u_HILOC (.Opcode(Opcode), .HiLoC(HiLoC));
  MemWriteC MemWriteC (.Opcode(Opcode), .Subop(Subop), .MemWrite(MemWrite));
  BRJRC BRJRC (.Opcode(Opcode), .BR(BR), .JR(JR));
endmodule

module RegWriteC (
  input  [3:0] Opcode,
  input  Subop,
  output RegWrite,
  output [2:0] WriteMUX
);

  wire and_1_out, and_2_out, and_3_out, and_4_out, and_5_out, and_6_out, and_7_out, not_1_out, not_2_out,
       not_3_out, not_4_out, not_5_out, not_6_out, not_7_out, not_8_out, not_9_out, not_10_out, not_11_out,
       not_12_out, not_13_out, not_14_out;

  not not_1 (not_1_out, Opcode[3]);
  not not_2 (not_2_out, Opcode[2]);
  not not_3 (not_3_out, Opcode[0]);
  not not_4 (not_4_out, Opcode[3]);
  not not_5 (not_5_out, Opcode[1]);
  not not_6 (not_6_out, Opcode[0]);
  not not_7 (not_7_out, Opcode[2]);
  not not_8 (not_8_out, Opcode[1]);
  not not_9 (not_9_out, Opcode[1]);
  not not_10 (not_10_out, Opcode[0]);
  not not_11 (not_11_out, Subop);
  not not_12 (not_12_out, Subop);
  not not_13 (not_13_out, Opcode[3]);
  not not_14 (not_14_out, Opcode[1]);
  and and_1 (and_1_out, Opcode[2], Subop);
  and and_2 (and_2_out, Opcode[3], Opcode[2]);
  and and_3 (and_3_out, not_1_out, not_2_out, not_3_out);
  and and_4 (and_4_out, not_4_out, not_5_out, not_6_out);
  and and_5 (and_5_out, not_7_out, not_8_out, Opcode[0]);
  and and_6 (and_6_out, Opcode[2], not_9_out, not_10_out, not_11_out);
  and and_7 (and_7_out, Opcode[3], Opcode[2], Opcode[1], Opcode[0], not_12_out);
  and and_8 (WriteMUX[2], not_13_out, Opcode[2]);
  and and_9 (WriteMUX[1], Opcode[3], not_14_out);
  or or_1 (WriteMUX[0], and_1_out, and_2_out);
  or or_2 (RegWrite, and_3_out, and_4_out, and_5_out, and_6_out, and_7_out);
endmodule

module ALUOpC (
  input  [3:0] Opcode,
  input  Subop,
  output [2:0] ALUop
);

  wire and_1_out, and_2_out, and_3_out, and_4_out, and_5_out, and_6_out, and_7_out, and_8_out, and_9_out,
       not_1_out, not_2_out, not_3_out, not_4_out, not_5_out, not_6_out, not_7_out, not_8_out, not_9_out,
       not_10_out, not_11_out, not_12_out, not_13_out, not_14_out;

  not not_1 (not_1_out, Opcode[3]);
  not not_2 (not_2_out, Opcode[2]);
  not not_3 (not_3_out, Opcode[0]);
  not not_4 (not_4_out, Opcode[3]);
  not not_5 (not_5_out, Opcode[2]);
  not not_6 (not_6_out, Opcode[1]);
  not not_7 (not_7_out, Opcode[2]);
  not not_8 (not_8_out, Opcode[0]);
  not not_9 (not_9_out, Opcode[0]);
  not not_10 (not_10_out, Opcode[3]);
  not not_11 (not_11_out, Opcode[2]);
  not not_12 (not_12_out, Opcode[3]);
  not not_13 (not_13_out, Opcode[1]);
  not not_14 (not_14_out, Opcode[0]);
  and and_1 (and_1_out, not_1_out, not_2_out, Opcode[0]);
  or or_1 (ALUop[2], and_1_out, and_2_out);
  and and_2 (and_2_out, Opcode[2], not_3_out);
  and and_3 (and_3_out, not_4_out, not_5_out, not_6_out, Opcode[0]);
  and and_4 (and_4_out, not_7_out, Opcode[1], not_8_out);
  and and_5 (and_5_out, Opcode[2], Opcode[1], Opcode[0]);
  and and_6 (and_6_out, Opcode[3], not_9_out);
  and and_7 (and_7_out, not_10_out, not_11_out, Subop);
  or or_2 (ALUop[0], and_7_out, and_8_out, and_9_out);
  and and_8 (and_8_out, not_12_out, Opcode[2], not_13_out);
  and and_9 (and_9_out, Opcode[3], not_14_out);
  or or_3 (ALUop[1], and_3_out, and_4_out, and_5_out, and_6_out);
endmodule

module Halt_Put (
  input  [3:0] Opcode,
  output Put,
  output Halt
);

  and and_1 (Put, ~Opcode[0], Opcode[1], ~Opcode[2], Opcode[3]);  // AND_Gate
  and and_2 (Halt, Opcode[0], Opcode[1], ~Opcode[2], Opcode[3]);  // AND_Gate
endmodule

module ALU (
  input  [15:0] rs,
  input  [15:0] rt,
  input  [7:0] Immediate,
  input  [2:0] Opcode,
  output Branch,
  output [15:0] Result,
  output [15:0] HI
);

  wire adder_1_cout, comparator_1_eq, comparator_2_eq, comparator_2_gt, comparator_2_lt, not_1_out,
       not_2_out, subtractor_1_bout;
  wire [15:0] adder_1_out, adder_2_out, adder_3_out, and_1_out, bit_extender_1_out, bit_extender_2_out,
       bit_extender_3_out, bit_extender_4_out, controlled_buffer_1_out, divider_1_out, divider_1_rem,
       multiplier_1_cout, multiplier_1_out, nor_1_out, subtractor_1_out;

  assign bit_extender_1_out = {{8{Immediate[7]}}, Immediate};  // Bit_Extender bit_extender_1
  assign bit_extender_2_out = {{8{1'b0}}, Immediate};  // Bit_Extender bit_extender_2
  Comparator #(.width(16)) comparator_1 (.a(rt), .b({16{1'b0}}), .eq(comparator_1_eq));  // open: gt, lt
  Comparator #(.width(16)) comparator_2 (
    .a(rs), .b({16{1'b0}}), .gt(comparator_2_gt), .eq(comparator_2_eq), .lt(comparator_2_lt));
  Adder #(.width(16)) adder_1 (.a(rs), .b(rt), .out(adder_1_out), .cin(1'b0), .cout(adder_1_cout));
  Subtractor #(.width(16)) subtractor_1 (.a(rs), .b(rt), .out(subtractor_1_out), .bin(1'b0), .bout(subtractor_1_bout));
  assign and_1_out = rs & rt;  // AND_Gate and_1, 16 bits wide
  assign nor_1_out = ~(rs | rt);  // NOR_Gate nor_1, 16 bits wide
  Divider #(.width(16)) divider_1 (.a(rs), .b(rt), .out(divider_1_out), .upper({16{1'b0}}), .rem(divider_1_rem));
  Multiplier #(.width(16)) multiplier_1 (
    .a(rs), .b(rt), .out(multiplier_1_out), .cin({16{1'b0}}), .cout(multiplier_1_cout));
  Adder #(.width(16)) adder_2 (.a(rs), .b(bit_extender_1_out), .out(adder_2_out), .cin(1'b0));  // open: cout
  Adder #(.width(16)) adder_3 (.a(rs), .b(bit_extender_2_out), .out(adder_3_out), .cin(1'b0));  // open: cout
  not not_1 (not_1_out, comparator_1_eq);
  assign controlled_buffer_1_out = not_1_out ? divider_1_out : 16'bz;  // Controlled_Buffer controlled_buffer_1
  not not_2 (not_2_out, comparator_2_eq);
  assign bit_extender_3_out = {{15{1'b0}}, adder_1_cout};  // Bit_Extender bit_extender_3
  assign bit_extender_4_out = {{15{1'b0}}, subtractor_1_bout};  // Bit_Extender bit_extender_4
  Multiplexer #(.select(3), .width(16), .enable("false")) multiplexer_1 (
    .in0(adder_1_out), .in1(subtractor_1_out), .in2(and_1_out), .in3(nor_1_out),
    .in4(controlled_buffer_1_out), .in5(multiplier_1_out), .in6(adder_2_out), .in7(adder_3_out),
    .out(Result), .sel(Opcode));
  Multiplexer #(.select(3), .disabled(0), .enable("false")) multiplexer_2 (
    .in0(1'b1), .in1(comparator_2_gt), .in2(not_2_out), .in3(comparator_2_eq), .in4(comparator_2_lt),
    .in5(1'b0), .in6(1'b0), .in7(1'b0), .out(Branch), .sel(Opcode));
  Multiplexer #(.select(3), .width(16), .enable("false")) multiplexer_3 (
    .in0(bit_extender_3_out), .in1(bit_extender_4_out), .in2({16{1'b0}}), .in3({16{1'b0}}),
    .in4(divider_1_rem), .in5(multiplier_1_cout), .in6(adder_2_out), .in7(adder_3_out), .out(HI), .sel(Opcode));

  // Notes on the sheet:
  //   Branch_Path
  //   Constant 1 is for absolute branches to imm
endmodule

module Fields (
  input  [15:0] Instruction,
  output [2:0] Rs,
  output [2:0] Rt,
  output [3:0] Opcode,
  output [7:0] Immediate,
  output Subop
);


  assign Immediate = Instruction[8:1];
  assign Opcode = Instruction[15:12];
  assign Rs = Instruction[11:9];
  assign Rt = Instruction[8:6];
  assign Subop = Instruction[0];
endmodule

module HILOC (
  input  [3:0] Opcode,
  output HiLoC
);

  wire and_1_out, and_2_out, not_1_out, not_2_out;

  not not_1 (not_1_out, Opcode[3]);
  not not_2 (not_2_out, Opcode[2]);
  and and_1 (and_1_out, not_1_out, not_2_out);
  and and_2 (and_2_out, Opcode[1], Opcode[0]);
  and and_3 (HiLoC, and_1_out, and_2_out);
endmodule

module MemWriteC (
  input  [3:0] Opcode,
  input  Subop,
  output MemWrite
);

  wire not_1_out;

  not not_1 (not_1_out, Opcode[1]);
  not not_2 (not_1_out, Opcode[0]);
  and and_1 (MemWrite, Opcode[3], Opcode[2], not_1_out, not_1_out, Subop);
endmodule

module BRJRC (
  input  [3:0] Opcode,
  output BR,
  output JR
);

  wire and_1_out, and_2_out, and_3_out, not_1_out, not_2_out, not_3_out, not_4_out, not_5_out;

  not not_1 (not_1_out, Opcode[1]);
  not not_2 (not_2_out, Opcode[3]);
  not not_3 (not_3_out, Opcode[2]);
  not not_4 (not_4_out, Opcode[1]);
  not not_5 (not_5_out, Opcode[0]);
  and and_1 (and_1_out, Opcode[2], not_1_out, Opcode[0]);
  and and_2 (and_2_out, not_2_out, Opcode[2], Opcode[1]);
  and and_3 (and_3_out, Opcode[3], not_3_out, not_4_out);
  and and_4 (JR, Opcode[3], Opcode[2], Opcode[1], not_5_out);
  or or_1 (BR, and_1_out, and_2_out, and_3_out);
endmodule
